# Fritzing sketch RaminPcbV1 (saved by Fritzing 0.9.3b)
circuit board: 3.40299cm x 3.7713cm
breadboards: 1

parts:
  zmpt101b = male pin header, 4 pins [form="♂ (male)"]
  pot = Trimmer Potentiometer [maximum_resistance=10kΩ package=THT]
  Part1 = Adafruit ADS1015 12Bit I2C ADC [part_number="Adafruit #1083"]
  1k_resistor = male pin header, 2 pins [form="♂ (male)"]
  pi = male pin header, 6 pins [form="♂ (male)"]

nets:
  N1: zmpt101b.pin1, pot.leg2, Part1.VDD, pi.pin1
  N2: zmpt101b.pin2, Part1.AIN1, Part1.AIN0
  N3: zmpt101b.pin4, pot.leg1, pot.wiper, Part1.ADDR, Part1.GND, 1k_resistor.pin1, 1k_resistor.pin2, pi.pin5
  N4: Part1.SDA, pi.pin2
  N5: Part1.SCL, pi.pin3

notes:
  vcc
  out
  GND
  Ramin
  OUT
  VCC
  PIN3
  PIN2
  3v3
  gnd
  5v
  sda
  scl

custom parts:
  Adafruit ADS1015 12Bit I2C ADC: For microcontrollers without an analog-to-digital converter or when you want a higher-precision ADC, the ADS1015 provides 12-bit precision at 3300 samples/second over I2C. The chip can be configured as 4 single-ended input channels, or two differential channels. As a nice bonus, it even includes a programmable gain amplifier, up to x16, to help boost up smaller single/differential signals to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
