# Fritzing sketch solarProjectwithParts (saved by Fritzing 0.9.3b)
breadboards: 1

parts:
  Raspberry_Pi_1 = Raspberry Pi 3 [part_number=RPI-3-V1.2]
  ACS712_Current_Sensor1 = ACS712 Current Sensor
  DS1 = DS18B20 1-Wire Temperature Sensor [part_number=DS18B20]
  R1 = Resistor [tolerance=±5% resistance=4.7k package=THT]
  R2 = Resistor [tolerance=±5% resistance=470 package=THT]
  R3 = Resistor [tolerance=±5% resistance=1k package=THT]
  J1 = female pin header, 3 pins [form="♀ (female)"]
  Part1 = Adafruit ADS1115 16Bit I2C ADC [part_number="Adafruit #1085"]
  D1 = SOLAR-IXYS [package=solarbit-12x1]
  J2 = female pin header, 2 pins [form="♀ (female)"]
  R4 = Resistor [tolerance=±5% resistance=100 package=THT]

nets:
  VDD: Raspberry_Pi_1.3v3, ACS712_Current_Sensor1.VCC, DS1.VDD, R1.Pin_1, J1.pin3, Part1.VDD
  N1: Raspberry_Pi_1.GPIO2, Part1.SDA
  N2: Raspberry_Pi_1.GPIO3, Part1.SCL
  N3: Raspberry_Pi_1.GIPO4, DS1.DQ, R1.Pin_0
  GND: Raspberry_Pi_1.GND, ACS712_Current_Sensor1.GND, DS1.GND, R3.Pin_1, J1.pin1, Part1.GND
  N4: ACS712_Current_Sensor1.OUT, R2.Pin_0
  N5: R2.Pin_1, R3.Pin_0, Part1.AIN1
  N6: J1.pin2, Part1.AIN0
  N7: D1.A, J2.pin2
  N8: D1.C, J2.pin1, R4.Pin_0

custom parts:
  ACS712 Current Sensor: A breakout board for the Allegro ACS712 is a Hall Effect-based linear current sensor. The module operates at 5V.
  Adafruit ADS1115 16Bit I2C ADC: For microcontrollers without an analog-to-digital converter or when you want a higher-precision ADC, the ADS1115 provides 16-bit precision at 860 samples/second over I2C. The chip can be configured as 4 single-ended input channels, or two differential channels. As a nice bonus, it even includes a programmable gain amplifier, up to x16, to help boost up smaller single/differential signals to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
